# Fritzing sketch Gas_sensor (saved by Fritzing 0.9.4)
breadboards: 1

parts:
  Parça1 = Arduino Uno (Rev3)
  J1 = Piezo Speaker
  Parça2 = Adafruit MiCS-5524 Gas Sensor [part_number="Adafruit #3199"]
  R1 = Resistor [tolerance=±5% resistance=380 package=THT]
  LED1 = LED - 3mm [color="Red (633nm)" package="3 mm [THT]"]
  R2 = Resistor [tolerance=±5% resistance=380 package=THT]

nets:
  N1: Parça1.A0, Parça2.AOUT
  N2: Parça1.D8, R2.Pin_1
  N3: Parça1.D7, R1.Pin_1
  N4: Parça1.5V, Parça2.5.0V
  GND: Parça1.GND, J1.pin1, Parça2.GND, LED1.cathode
  N5: J1.pin2, R1.Pin_0
  N6: LED1.anode, R2.Pin_0

custom parts:
  Adafruit MiCS-5524 Gas Sensor: Give your next sensor project a nose for gasses with the Adafruit MiCS-5524 Gas Sensor Breakout. This breakout makes it easy to use this nice sensor from SGX Sensortech. The MiCS-5524 is a robust MEMS sensor for indoor carbon monoxide and natural gas leakage detection, it's suitable also for indoor air quality monitoring; breath checker and early fire detection. Please note: This sensor is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
